// Logisim project NAND_transistors.circ as structural Verilog: 1 circuit, main circuit main
module main (
  input  PR,
  input  J,
  input  CLK,
  input  K,
  input  CLR,
  input  in_6,
  input  NOT,
  input  in_8,
  input  in_9,
  input  in_10,
  input  in_11,
  input  in_12,
  input  in_13,
  input  in_14,
  input  in_15,
  input  in_16,
  input  in_17,
  input  in_18,
  output Q,
  output out_20,
  output out_21,
  output out_22,
  output out_23,
  output out_24,
  output out_25,
  output out_26,
  output out_27
);

  wire and_1_out, and_2_out, and_3_out, and_4_out, nor_1_out, nor_2_out, not_1_out, transistor_2_out,
       transistor_4_out, transistor_5_out, transistor_7_out, transistor_8_out, transistor_10_out,
       transistor_11_out, transistor_13_out, transistor_15_out, transistor_17_out, transistor_19_out,
       transistor_20_out, transistor_23_out, transistor_25_out, transistor_26_out, transistor_28_out,
       transistor_29_out, transistor_32_out, transistor_33_out, transistor_34_out, transistor_45_out,
       transistor_49_out, transistor_50_out, transistor_52_out, transistor_53_out, transistor_55_out,
       transistor_56_out, transistor_58_out, transistor_59_out, transistor_61_out, transistor_62_out,
       transistor_64_out, transistor_65_out, transistor_67_out, transistor_68_out, transistor_70_out,
       transistor_71_out, transistor_73_out, transistor_74_out, transistor_86_out, transistor_88_out,
       transistor_92_out, transistor_94_out, transistor_96_out, transistor_103_out, undriven, undriven_2,
       undriven_3, undriven_4, undriven_5, undriven_6, undriven_7, undriven_8, undriven_9, undriven_10;

  Transistor #(.\type ("n")) transistor_1 (.in(transistor_2_out), .out(out_21), .gate(in_8));
  Transistor #(.\type ("n")) transistor_2 (.in(1'b0), .out(transistor_2_out), .gate(in_6));
  Transistor transistor_3 (.in(1'b1), .out(out_21), .gate(in_8));
  Transistor #(.\type ("n")) transistor_4 (.in(transistor_5_out), .out(transistor_4_out), .gate(in_9));
  Transistor #(.\type ("n")) transistor_5 (.in(1'b0), .out(transistor_5_out), .gate(in_9));
  Transistor transistor_6 (.in(1'b1), .out(transistor_4_out), .gate(in_9));
  Transistor #(.\type ("n")) transistor_7 (.in(transistor_8_out), .out(transistor_7_out), .gate(in_10));
  Transistor #(.\type ("n")) transistor_8 (.in(1'b0), .out(transistor_8_out), .gate(in_10));
  Transistor transistor_9 (.in(1'b1), .out(transistor_7_out), .gate(in_10));
  Transistor #(.\type ("n")) transistor_10 (.in(transistor_11_out), .out(transistor_10_out), .gate(in_12));
  Transistor #(.\type ("n")) transistor_11 (.in(1'b0), .out(transistor_11_out), .gate(in_11));
  Transistor transistor_12 (.in(1'b1), .out(transistor_10_out), .gate(in_12));
  Transistor #(.\type ("n")) transistor_13 (.in(transistor_32_out), .out(transistor_13_out), .gate(in_13));
  Transistor transistor_14 (.in(1'b1), .out(transistor_13_out), .gate(in_13));
  Transistor #(.\type ("n")) transistor_15 (.in(transistor_33_out), .out(transistor_15_out), .gate(in_14));
  Transistor transistor_16 (.in(1'b1), .out(transistor_15_out), .gate(in_14));
  Transistor #(.\type ("n")) transistor_17 (.in(transistor_34_out), .out(transistor_17_out), .gate(in_13));
  Transistor transistor_18 (.in(1'b1), .out(transistor_17_out), .gate(in_13));
  Transistor #(.\type ("n")) transistor_19 (.in(transistor_20_out), .out(transistor_19_out), .gate(in_16));
  Transistor #(.\type ("n")) transistor_20 (.in(1'b0), .out(transistor_20_out), .gate(in_15));
  Transistor transistor_21 (.in(1'b1), .out(transistor_19_out), .gate(in_16));
  Transistor #(.\type ("n")) transistor_22 (.in(transistor_23_out), .out(out_27), .gate(in_18));
  Transistor #(.\type ("n")) transistor_23 (.in(1'b0), .out(transistor_23_out), .gate(in_17));
  Transistor transistor_24 (.in(1'b1), .out(out_27), .gate(in_18));
  Transistor #(.\type ("n")) transistor_25 (.in(transistor_26_out), .out(transistor_25_out), .gate(undriven_3));
  Transistor #(.\type ("n")) transistor_26 (.in(1'b0), .out(transistor_26_out), .gate(undriven));
  Transistor transistor_27 (.in(1'b1), .out(transistor_25_out), .gate(undriven_3));
  Transistor #(.\type ("n")) transistor_28 (.in(transistor_29_out), .out(transistor_28_out), .gate(undriven_4));
  Transistor #(.\type ("n")) transistor_29 (.in(1'b0), .out(transistor_29_out), .gate(undriven_2));
  Transistor transistor_30 (.in(1'b1), .out(transistor_28_out), .gate(undriven_4));
  and and_1 (and_1_out, out_20, CLK);
  and and_2 (and_2_out, CLK, Q);
  Transistor transistor_31 (.in(1'b1), .out(out_21), .gate(in_6));
  Transistor #(.\type ("n")) transistor_32 (.in(1'b0), .out(transistor_32_out), .gate(in_13));
  Transistor #(.\type ("n")) transistor_33 (.in(1'b0), .out(transistor_33_out), .gate(in_14));
  Transistor #(.\type ("n")) transistor_34 (.in(1'b0), .out(transistor_34_out), .gate(in_14));
  Transistor transistor_35 (.in(1'b1), .out(transistor_19_out), .gate(in_15));
  not not_1 (not_1_out, CLK);
  Transistor transistor_36 (.in(1'b1), .out(transistor_4_out), .gate(in_9));
  Transistor transistor_37 (.in(1'b1), .out(transistor_7_out), .gate(in_10));
  Transistor transistor_38 (.in(1'b1), .out(transistor_10_out), .gate(in_11));
  Transistor transistor_39 (.in(1'b1), .out(transistor_13_out), .gate(in_13));
  Transistor transistor_40 (.in(1'b1), .out(transistor_15_out), .gate(in_14));
  Transistor transistor_41 (.in(1'b1), .out(transistor_17_out), .gate(in_14));
  Transistor transistor_42 (.in(1'b1), .out(out_27), .gate(in_17));
  Transistor transistor_43 (.in(1'b1), .out(transistor_25_out), .gate(undriven));
  Transistor transistor_44 (.in(1'b1), .out(transistor_28_out), .gate(undriven_2));
  nor nor_1 (nor_1_out, PR, and_1_out, nor_2_out);
  nor nor_2 (nor_2_out, nor_1_out, and_2_out, CLR);
  Transistor #(.\type ("n")) transistor_45 (.in(transistor_73_out), .out(transistor_45_out), .gate(transistor_15_out));
  Transistor transistor_46 (.in(1'b1), .out(transistor_45_out), .gate(transistor_15_out));
  Transistor #(.\type ("n")) transistor_47 (.in(transistor_74_out), .out(out_25), .gate(transistor_17_out));
  Transistor transistor_48 (.in(1'b1), .out(out_25), .gate(transistor_17_out));
  Transistor #(.\type ("n")) transistor_49 (.in(transistor_50_out), .out(transistor_49_out), .gate(transistor_19_out));
  Transistor #(.\type ("n")) transistor_50 (.in(1'b0), .out(transistor_50_out), .gate(in_15));
  Transistor transistor_51 (.in(1'b1), .out(transistor_49_out), .gate(transistor_19_out));
  Transistor #(.\type ("n")) transistor_52 (.in(transistor_53_out), .out(transistor_52_out), .gate(in_16));
  Transistor #(.\type ("n")) transistor_53 (.in(1'b0), .out(transistor_53_out), .gate(transistor_19_out));
  Transistor transistor_54 (.in(1'b1), .out(transistor_52_out), .gate(in_16));
  Transistor #(.\type ("n")) transistor_55 (.in(transistor_56_out), .out(transistor_55_out), .gate(undriven_8));
  Transistor #(.\type ("n")) transistor_56 (.in(1'b0), .out(transistor_56_out), .gate(undriven_5));
  Transistor transistor_57 (.in(1'b1), .out(transistor_55_out), .gate(undriven_8));
  Transistor #(.\type ("n")) transistor_58 (.in(transistor_59_out), .out(transistor_58_out), .gate(undriven_9));
  Transistor #(.\type ("n")) transistor_59 (.in(1'b0), .out(transistor_59_out), .gate(undriven_6));
  Transistor transistor_60 (.in(1'b1), .out(transistor_58_out), .gate(undriven_9));
  Transistor #(.\type ("n")) transistor_61 (.in(transistor_62_out), .out(transistor_61_out), .gate(undriven_10));
  Transistor #(.\type ("n")) transistor_62 (.in(1'b0), .out(transistor_62_out), .gate(undriven_7));
  Transistor transistor_63 (.in(1'b1), .out(transistor_61_out), .gate(undriven_10));
  Transistor #(.\type ("n")) transistor_64 (.in(transistor_65_out), .out(transistor_64_out), .gate(transistor_7_out));
  Transistor #(.\type ("n")) transistor_65 (.in(1'b0), .out(transistor_65_out), .gate(transistor_4_out));
  Transistor transistor_66 (.in(1'b1), .out(transistor_64_out), .gate(transistor_7_out));
  Transistor #(.\type ("n")) transistor_67 (.in(transistor_68_out), .out(transistor_67_out), .gate(transistor_10_out));
  Transistor #(.\type ("n")) transistor_68 (.in(1'b0), .out(transistor_68_out), .gate(in_11));
  Transistor transistor_69 (.in(1'b1), .out(transistor_67_out), .gate(transistor_10_out));
  Transistor #(.\type ("n")) transistor_70 (.in(transistor_71_out), .out(transistor_70_out), .gate(in_12));
  Transistor #(.\type ("n")) transistor_71 (.in(1'b0), .out(transistor_71_out), .gate(transistor_10_out));
  Transistor transistor_72 (.in(1'b1), .out(transistor_70_out), .gate(in_12));
  Transistor #(.\type ("n")) transistor_73 (.in(1'b0), .out(transistor_73_out), .gate(transistor_13_out));
  Transistor #(.\type ("n")) transistor_74 (.in(1'b0), .out(transistor_74_out), .gate(transistor_45_out));
  and and_3 (and_3_out, nor_1_out, not_1_out);
  and and_4 (and_4_out, not_1_out, nor_2_out);
  Transistor transistor_75 (.in(1'b1), .out(transistor_64_out), .gate(transistor_4_out));
  Transistor transistor_76 (.in(1'b1), .out(transistor_67_out), .gate(in_11));
  Transistor transistor_77 (.in(1'b1), .out(transistor_70_out), .gate(transistor_10_out));
  Transistor transistor_78 (.in(1'b1), .out(transistor_45_out), .gate(transistor_13_out));
  Transistor transistor_79 (.in(1'b1), .out(out_25), .gate(transistor_45_out));
  Transistor transistor_80 (.in(1'b1), .out(transistor_49_out), .gate(in_15));
  Transistor transistor_81 (.in(1'b1), .out(transistor_52_out), .gate(transistor_19_out));
  Transistor transistor_82 (.in(1'b1), .out(transistor_55_out), .gate(undriven_5));
  Transistor transistor_83 (.in(1'b1), .out(transistor_58_out), .gate(undriven_6));
  Transistor transistor_84 (.in(1'b1), .out(transistor_61_out), .gate(undriven_7));
  Transistor #(.\type ("n")) transistor_85 (.in(transistor_86_out), .out(out_22), .gate(NOT));
  Transistor #(.\type ("n")) transistor_86 (.in(1'b0), .out(transistor_86_out), .gate(NOT));
  Transistor transistor_87 (.in(1'b1), .out(out_22), .gate(NOT));
  Transistor #(.\type ("n")) transistor_88 (.in(transistor_92_out), .out(transistor_88_out), .gate(transistor_52_out));
  Transistor transistor_89 (.in(1'b1), .out(transistor_88_out), .gate(transistor_52_out));
  nand nand_1 (Q, and_3_out, out_20);
  nand nand_2 (out_20, Q, and_4_out);
  Transistor #(.\type ("n")) transistor_90 (.in(transistor_94_out), .out(out_23), .gate(transistor_64_out));
  Transistor transistor_91 (.in(1'b1), .out(out_23), .gate(transistor_64_out));
  Transistor #(.\type ("n")) transistor_92 (.in(1'b0), .out(transistor_92_out), .gate(transistor_49_out));
  Transistor transistor_93 (.in(1'b1), .out(out_22), .gate(NOT));
  Transistor #(.\type ("n")) transistor_94 (.in(1'b0), .out(transistor_94_out), .gate(transistor_64_out));
  Transistor #(.\type ("n")) transistor_95 (.in(transistor_96_out), .out(out_24), .gate(transistor_70_out));
  Transistor #(.\type ("n")) transistor_96 (.in(1'b0), .out(transistor_96_out), .gate(transistor_67_out));
  Transistor transistor_97 (.in(1'b1), .out(out_24), .gate(transistor_70_out));
  Transistor transistor_98 (.in(1'b1), .out(transistor_88_out), .gate(transistor_49_out));
  Transistor transistor_99 (.in(1'b1), .out(out_23), .gate(transistor_64_out));
  Transistor transistor_100 (.in(1'b1), .out(out_24), .gate(transistor_67_out));
  Transistor #(.\type ("n")) transistor_101 (.in(transistor_103_out), .out(out_26), .gate(transistor_88_out));
  Transistor transistor_102 (.in(1'b1), .out(out_26), .gate(transistor_88_out));
  Transistor #(.\type ("n")) transistor_103 (.in(1'b0), .out(transistor_103_out), .gate(transistor_88_out));
  Transistor transistor_104 (.in(1'b1), .out(out_26), .gate(transistor_88_out));

  // Notes on the sheet:
  //   XOR
  //   XNOR
  //   NAND
  //   NOR
  //   XNOR
  //   Standard cells: https://www.youtube.com/watch?v=yLqLD8Y4-Qc
endmodule
