// Logisim project compy.circ as structural Verilog: 1 circuit, main circuit main
module main (
  input  in_1,
  input  in_2,
  input  [2:0] in_3,
  input  in_4,
  input  in_5,
  output out_6,
  output out_7,
  output out_8
);

  wire and_1_out, or_1_out, xnor_1_out, xor_1_out, xor_2_out;

  xor xor_1 (xor_1_out, in_5, in_1);
  and and_1 (and_1_out, in_4, in_5);
  or or_1 (or_1_out, in_4, in_5);
  xor xor_2 (xor_2_out, in_4, in_5);
  xnor xnor_1 (xnor_1_out, in_4, in_5);
  Adder #(.width(1)) adder_1 (.a(in_4), .b(xor_1_out), .out(out_8), .cin(in_2), .cout(out_7));
  Multiplexer #(.select(3), .enable("false")) multiplexer_1 (
    .in0(and_1_out), .in1(or_1_out), .in2(xor_2_out), .in3(xnor_1_out), .in4(out_8), .out(out_6), .sel(in_3));  // open: in5, in6, in7
endmodule
