// Digital circuit digipooper.dig as structural Verilog
module digipooper (
  input  in_1,
  input  in_2,
  input  in_3,
  input  in_4,
  input  in_5,
  input  in_6,
  input  clk,
  input  in_8,
  input  clk_2,
  input  in_10,
  input  clk_3,
  input  in_12,
  input  in_13,
  input  clk_4,
  input  in_15,
  input  in_16,
  input  clk_5,
  input  in_18,
  input  clk_6,
  input  in_20,
  input  in_21
);

  wire A_Register, add_1_c_o, ALU_Output_Register, B_Register, counterpreset_1_ovf, Display_Register,
       Input_Register, IR, IR_Set, MAR, PC, PC_Set, register_3_q, register_4_q, ROM;
  wire [2:0] add_1_s, ALUReg, AReg, BReg, dipswitch_14_out, dipswitch_17_out, dipswitch_20_out,
       dipswitch_23_out, dipswitch_26_out, DisplayReg, driver_1_out, InputReg, InstReg, MAR_Value, PC_Value,
       register_5_q, register_6_q, register_7_q, register_8_q, rom_1_d, ROM_Data;
  wire [7:0] rom_2_d, rom_3_d, rom_5_d;

  DipSwitch dipswitch_1 (.out(Input_Register));
  DipSwitch dipswitch_2 (.out(IR_Set));
  DipSwitch dipswitch_3 (.out(IR));
  DipSwitch dipswitch_4 (.out(PC_Set));
  DipSwitch dipswitch_5 (.out(PC));
  DipSwitch dipswitch_6 (.out(MAR));
  DipSwitch dipswitch_7 (.out(ROM));
  DipSwitch dipswitch_8 (.out(A_Register));
  DipSwitch dipswitch_9 (.out(B_Register));
  DipSwitch dipswitch_10 (.out(ALU_Output_Register));
  DipSwitch dipswitch_11 (.out(Display_Register));
  // Probe on InputReg
  // Probe on InstReg
  // Probe on PC_Value
  // Probe on MAR_Value
  // Probe on ROM_Data
  // Probe on AReg
  // Probe on BReg
  // Probe on ALUReg
  // Probe on DisplayReg
  DipSwitch dipswitch_12 (.out(dipswitch_14_out[1]));
  DipSwitch dipswitch_13 (.out(dipswitch_14_out[2]));
  DipSwitch dipswitch_14 (.out(dipswitch_14_out[0]));
  DipSwitch dipswitch_15 (.out(dipswitch_17_out[1]));
  DipSwitch dipswitch_16 (.out(dipswitch_17_out[2]));
  DipSwitch dipswitch_17 (.out(dipswitch_17_out[0]));
  DipSwitch dipswitch_18 (.out(dipswitch_20_out[1]));
  DipSwitch dipswitch_19 (.out(dipswitch_20_out[2]));
  DipSwitch dipswitch_20 (.out(dipswitch_20_out[0]));
  DipSwitch dipswitch_21 (.out(dipswitch_23_out[1]));
  DipSwitch dipswitch_22 (.out(dipswitch_23_out[2]));
  DipSwitch dipswitch_23 (.out(dipswitch_23_out[0]));
  DipSwitch dipswitch_24 (.out(dipswitch_26_out[1]));
  DipSwitch dipswitch_25 (.out(dipswitch_26_out[2]));
  DipSwitch dipswitch_26 (.out(dipswitch_26_out[0]));
  CounterPreset #(.maxValue(8), .Bits(3), .isProgramCounter("true")) counterpreset_1 (
    .en(in_20), .C(clk_6), .dir(1'b0), .in(driver_1_out), .ld(PC_Set), .clr(in_21), .out(PC_Value),
    .ovf(counterpreset_1_ovf));
  Register #(.Bits(3)) register_1 (.D(driver_1_out), .C(clk_6), .en(IR_Set), .Q(InstReg));
  Register #(.Bits(3)) register_2 (.D(dipswitch_14_out), .C(clk_6), .en(1'b1), .Q(InputReg));
  LED led_1 (.in(in_1));
  Register register_3 (.D(in_2), .C(in_3), .en(in_4), .Q(register_3_q));
  Register register_4 (.D(in_5), .C(clk), .en(in_6), .Q(register_4_q));
  Register #(.Bits(3)) register_5 (.D(dipswitch_17_out), .C(clk_2), .en(in_8), .Q(register_5_q));
  Register #(.Bits(3)) register_6 (.D(dipswitch_20_out), .C(clk_3), .en(in_10), .Q(register_6_q));
  Register #(.Bits(3)) register_7 (.D(dipswitch_23_out), .C(clk_4), .en(in_13), .Q(register_7_q));
  Register #(.Bits(3)) register_8 (.D(dipswitch_26_out), .C(clk_5), .en(in_16), .Q(register_8_q));
  LED led_2 (.in(counterpreset_1_ovf));
  LED led_3 (.in(register_5_q[2]));
  LED led_4 (.in(register_6_q[2]));
  LED led_5 (.in(register_7_q[2]));
  LED led_6 (.in(register_8_q[2]));
  assign driver_1_out = PC ? PC_Value : 3'bz;  // Driver driver_1
  assign driver_1_out = IR ? InstReg : 3'bz;  // Driver driver_2
  assign driver_1_out = Input_Register ? InputReg : 3'bz;  // Driver driver_3
  LED led_7 (.in(register_3_q));
  LED led_8 (.in(register_4_q));
  LED led_9 (.in(register_5_q[0]));
  LED led_10 (.in(register_5_q[1]));
  LED led_11 (.in(register_6_q[0]));
  LED led_12 (.in(register_6_q[1]));
  LED led_13 (.in(register_7_q[0]));
  LED led_14 (.in(register_7_q[1]));
  LED led_15 (.in(register_8_q[0]));
  LED led_16 (.in(register_8_q[1]));
  ROM #(.AddrBits(3), .Bits(3)) rom_1 (.A(register_6_q), .sel(in_12), .D(rom_1_d));
  ROM #(.AddrBits(3), .Bits(8)) rom_2 (.A(register_7_q), .sel(in_15), .D(rom_2_d));
  ROM #(.AddrBits(3), .Bits(8)) rom_3 (.A(register_8_q), .sel(in_18), .D(rom_3_d));
  LED led_17 (.in(rom_1_d[2]));
  assign driver_1_out = ROM ? ROM_Data : 3'bz;  // Driver driver_4
  LED led_18 (.in(rom_1_d[0]));
  LED led_19 (.in(rom_1_d[1]));
  ROM #(.AddrBits(3), .Bits(3)) rom_4 (.A(MAR_Value), .sel(1'b1), .D(ROM_Data));
  assign driver_1_out = ALU_Output_Register ? ALUReg : 3'bz;  // Driver driver_5
  Seven_Seg seven_seg_1 (
    .a(rom_2_d[4]), .b(rom_2_d[5]), .c(rom_2_d[6]), .d(rom_2_d[7]), .e(rom_2_d[3]), .f(rom_2_d[2]),
    .g(rom_2_d[1]), .dp(rom_2_d[0]));
  Seven_Seg seven_seg_2 (
    .a(rom_3_d[4]), .b(rom_3_d[5]), .c(rom_3_d[6]), .d(rom_3_d[7]), .e(rom_3_d[3]), .f(rom_3_d[2]),
    .g(rom_3_d[1]), .dp(rom_3_d[0]));
  Register #(.Bits(3)) register_9 (.D(add_1_s), .C(clk_6), .en(1'b1), .Q(ALUReg));
  Register #(.Bits(3)) register_10 (.D(driver_1_out), .C(clk_6), .en(MAR), .Q(MAR_Value));
  Register #(.Bits(3)) register_11 (.D(driver_1_out), .C(clk_6), .en(Display_Register), .Q(DisplayReg));
  Register #(.Bits(3)) register_12 (.D(driver_1_out), .C(clk_6), .en(A_Register), .Q(AReg));
  Register #(.Bits(3)) register_13 (.D(driver_1_out), .C(clk_6), .en(B_Register), .Q(BReg));
  ROM #(.AddrBits(3), .Bits(8)) rom_5 (.A(DisplayReg), .sel(1'b1), .D(rom_5_d));
  Add #(.Bits(3)) add_1 (.a(AReg), .b(BReg), .c_i(1'b0), .s(add_1_s), .c_o(add_1_c_o));
  Seven_Seg seven_seg_3 (
    .a(rom_5_d[4]), .b(rom_5_d[5]), .c(rom_5_d[6]), .d(rom_5_d[7]), .e(rom_5_d[3]), .f(rom_5_d[2]),
    .g(rom_5_d[1]), .dp(rom_5_d[0]));
  LED led_20 (.in(add_1_c_o));

  // Other names for the same wires on the sheet: System_clock = clk_6

  // Notes on the sheet:
  //   clk: Hz: 2
  //   clk_2: Hz: 2
  //   clk_3: Hz: 2
  //   clk_4: Hz: 2
  //   in_15: default 1
  //   clk_5: Hz: 2
  //   in_18: default 1
  //   clk_6: Hz: 2
  //   ALU Control
  //   Simple
  //   Register
  //   Register with clock
  //   Register with clock, 3-bit
  //   Memory register with ROM
  //   Data
  //   Bus
  //   contents of rom_1 (hex, n*v repeats v):
  //   0,1,2,3,4,5,6,7
  //   contents of rom_2 (hex, n*v repeats v):
  //   fc,60,ba,f2,66,d6,de,70
  //   contents of rom_3 (hex, n*v repeats v):
  //   fc,60,ba,f2,66,d6,de,70
  //   contents of rom_4 (hex, n*v repeats v):
  //   0,1,2,3,4,5,4,5
  //   ROM 3-bit data
  //   Address          Value
  //   0x0	0b000
  //   0x1	0b001
  //   0x2	0b010
  //   0x3	0b011
  //   0x4	0b100
  //   0x5	0b101
  //   0x6	0b110
  //   0x7	0b111
  //   ROM 8-bit data
  //   Address          Value
  //   0x0	0b11111100
  //   0x1	0b01100000
  //   0x2	0b10111010
  //   0x3	0b11110010
  //   0x4	0b01100110
  //   0x5	0b11010110
  //   0x6	0b11011110
  //   0x7	0b01110000
  //   contents of rom_5 (hex, n*v repeats v):
  //   fc,60,ba,f2,66,d6,de,70
endmodule
