// Logisim project alu.circ as structural Verilog
module main (
  input  [2:0] Sel,
  input  Cin,
  input  A,
  input  B,
  input  Sub,
  input  Less,
  output Result,
  output Set,
  output Cout
);

  wire and_1_out, nor_1_out, or_1_out, xor_1_out, xor_2_out;

  and and_1 (and_1_out, A, B);
  or or_1 (or_1_out, A, B);
  xor xor_1 (xor_1_out, A, B);
  nor nor_1 (nor_1_out, A, B);
  xor xor_2 (xor_2_out, B, Sub);
  Adder #(.width(1)) adder_1 (.a(A), .b(xor_2_out), .out(Set), .cin(Cin), .cout(Cout));
  Multiplexer #(.select(3)) multiplexer_1 (
    .in0(and_1_out), .in1(or_1_out), .in2(xor_1_out), .in3(nor_1_out), .in4(Set), .in5(Less), .out(Result),
    .sel(Sel));  // open: in6, in7

  // Notes on the sheet:
  //   https://www.youtube.com/watch?v=dYZ-Hwbcnq4
  //   000 AND
  //   001 OR
  //   010 XOR
  //   011 NOR
  //   100 ADD/SUB
endmodule

// VHDL entity temp, as the project stores it:
--------------------------------------------------------------------------------
-- Project :
-- File    :
-- Autor   :
-- Date    :
--
--------------------------------------------------------------------------------
-- Description :
--
--------------------------------------------------------------------------------

LIBRARY ieee;
USE ieee.std_logic_1164.all;

ENTITY temp IS
  PORT (
  ------------------------------------------------------------------------------
  --Insert input ports below
    clock      : IN  std_logic;                    -- input bit example
    val        : IN  std_logic_vector(3 DOWNTO 0); -- input vector example
  ------------------------------------------------------------------------------
  --Insert output ports below
    max        : OUT std_logic;                    -- output bit example
    cpt        : OUT std_logic_vector(3 DOWNTO 0)  -- output vector example
    );
END temp;

--------------------------------------------------------------------------------
--Complete your VHDL description below
--------------------------------------------------------------------------------

ARCHITECTURE TypeArchitecture OF temp IS

BEGIN


END TypeArchitecture;
