// Digital circuit macro.dig as structural Verilog
module macro (
  input  in_1,
  input  in_2,
  input  in_3,
  input  in_4,
  input  in_5,
  input  in_6,
  input  in_7,
  input  in_8,
  input  in_9,
  input  clk,
  input  in_11
);

  wire _74157_1_p13, _74157_1_p14, _74157_1_p15, _74157_1_p16, _74175_1_p9, _74175_1_p10, _74175_1_p11,
       _74175_1_p12, not_1_out;

  // _74157 _74157_1: pin names not known; wires that end beside it: in_1, in_2, in_3, in_4, in_5, in_6, in_7, in_8, in_9, clk, 1'b1, 1'b0, _74157_1_p13, _74157_1_p14, _74157_1_p15, _74157_1_p16
  not not_1 (not_1_out, clk);
  // _74175 _74175_1: pin names not known; wires that end beside it: not_1_out, in_11, _74157_1_p13, _74157_1_p14, _74157_1_p15, _74157_1_p16, 1'b1, 1'b0, _74175_1_p9, _74175_1_p10, _74175_1_p11, _74175_1_p12
  LED led_1 (.in(_74175_1_p9));
  LED led_2 (.in(_74175_1_p10));
  LED led_3 (.in(_74175_1_p11));
  LED led_4 (.in(_74175_1_p12));

  // Notes on the sheet:
  //   in_1: default 1
  //   in_2: default 1
  //   in_3: default 1
  //   in_4: default 1
  //   in_5: default 1
  //   in_6: default 1
  //   in_7: default 1
  //   in_8: default 1
  //   in_9: default 1
  //   in_11: default 1
endmodule
