// Logisim project temp.circ as structural Verilog: 1 circuit, main circuit main
module main (
  input  Sub,
  input  Cin,
  input  [2:0] in_3,
  input  A,
  input  B,
  output Result,
  output Cout,
  output Set
);

  wire and_1_out, or_1_out, xnor_1_out, xor_1_out, xor_2_out;

  xor xor_1 (xor_1_out, B, Sub);
  and and_1 (and_1_out, A, B);
  or or_1 (or_1_out, A, B);
  xor xor_2 (xor_2_out, A, B);
  xnor xnor_1 (xnor_1_out, A, B);
  Adder #(.width(1)) adder_1 (.a(A), .b(xor_1_out), .out(Set), .cin(Cin), .cout(Cout));
  Multiplexer #(.select(3), .enable("false")) multiplexer_1 (
    .in0(and_1_out), .in1(or_1_out), .in2(xor_2_out), .in3(xnor_1_out), .in4(Set), .out(Result), .sel(in_3));  // open: in5, in6, in7
endmodule
