// Digital circuit bit-slice-chips.dig as structural Verilog
module bit_slice_chips (
  input  clk,
  input  in_2,
  input  in_25,
  input  in_26,
  input  in_27,
  input  in_28,
  input  in_39,
  input  in_40,
  input  clk_2,
  output out_3,
  output out_4,
  output out_5,
  output out_6,
  output out_7,
  output out_8,
  output out_9,
  output out_10,
  output out_11,
  output out_12,
  output out_13,
  output out_14,
  output out_15,
  output out_16,
  output out_17,
  output out_18,
  output out_19,
  output out_20,
  output out_21,
  output out_22,
  output out_23,
  output out_24,
  output out_29,
  output out_30,
  output out_31,
  output out_32,
  output out_33,
  output out_34,
  output out_35,
  output out_36,
  output out_37,
  output out_38
);

  wire ADDER_OUT, AND_OUT, CARRY_IN, CARRY_OUT, driver_17_out, driver_49_out, driver_67_out, driver_83_out,
       driver_102_out, driver_118_out, driver_136_out, driver_152_out, driver_171_out, driver_187_out,
       driver_208_out, driver_225_out, driver_253_out, driver_282_out, driver_312_out, DS0_IN, DS0_OUT,
       DS1_IN, DS1_OUT, DS2_IN, DS2_OUT, DS3_IN, DS3_OUT, LOADREG, MUX0_OUT, MUX1_OUT, MUX_OUT, MUXSEL_A,
       MUXSEL_B, MUXSEL_C, MUXSEL_D, NAND_OUT, not_1_out, not_2_out, NOT_OUT, OR_OUT, pulldown_2_out,
       pulldown_4_out, pulldown_5_out, pulldown_7_out, pulldown_10_out, pulldown_11_out, pulldown_14_out,
       pulldown_15_out, pulldown_18_out, pulldown_19_out, pulldown_22_out, pulldown_23_out, pulldown_24_out,
       pulldown_26_out, pulldown_28_out, pulldown_30_out, pulldown_33_out, REG_IN0, REG_IN1, REG_IN2,
       REG_IN3, REG_IN4, REG_IN5, REG_IN6, REG_IN7, REG_OUT5, REG_OUT6, REG_OUT7, RESET, STACKDIRSEL, XOR_OUT;
  wire [1:0] dipswitch_1_out, eeprom_1_d;
  wire [3:0] counter_1_out;

  DipSwitch dipswitch_1 (.out(dipswitch_1_out[0]));
  DipSwitch dipswitch_2 (.out(dipswitch_1_out[1]));
  DipSwitch dipswitch_3 (.out(REG_IN7));
  DipSwitch dipswitch_4 (.out(REG_IN6));
  DipSwitch dipswitch_5 (.out(REG_IN5));
  Button #(.activeLow("true")) LOAD_IR (.out(LOADREG));
  DipSwitch u_MUXSEL_D (.out(REG_IN3));
  DipSwitch STACK_UP_DOWN (.out(REG_IN4));
  EEPROM #(.Bits(2)) eeprom_1 (.A(dipswitch_1_out), .CS(1'b1), .WE(1'b0), .OE(1'b1), .D(eeprom_1_d));
  DipSwitch u_MUXSEL_C (.out(REG_IN2));
  DipSwitch u_MUXSEL_B (.out(REG_IN1));
  DipSwitch u_MUXSEL_A (.out(REG_IN0));
  LED led_1 (.in(eeprom_1_d[0]));
  LED led_2 (.in(eeprom_1_d[1]));
  Button #(.activeLow("true")) u_RESET (.out(RESET));
  PullDown pulldown_1 (.out(CARRY_IN));
  LED led_3 (.in(DS0_OUT));
  LED led_4 (.in(DS1_OUT));
  LED led_5 (.in(DS2_OUT));
  LED led_6 (.in(DS3_OUT));
  Add add_1 (.a(DS0_OUT), .b(DS1_OUT), .c_i(CARRY_IN), .s(ADDER_OUT), .c_o(CARRY_OUT));
  _7408 AND_gate (
    .pin1(DS0_OUT), .pin2(DS1_OUT), .pin3(AND_OUT), .pin4(1'b0), .pin5(1'b0), .pin7(1'b0), .pin9(1'b0),
    .pin10(1'b0), .pin12(1'b0), .pin13(1'b0), .pin14(1'b1));  // open: pin6, pin8, pin11
  PullUp pullup_1 (.out(RESET));
  _74273 _8_bit_register (
    .pin1(RESET), .pin2(MUXSEL_A), .pin3(REG_IN0), .pin4(REG_IN1), .pin5(MUXSEL_B), .pin6(MUXSEL_C),
    .pin7(REG_IN2), .pin8(REG_IN3), .pin9(MUXSEL_D), .pin10(1'b0), .pin11(LOADREG), .pin12(STACKDIRSEL),
    .pin13(REG_IN4), .pin14(REG_IN5), .pin15(REG_OUT5), .pin16(REG_OUT6), .pin17(REG_IN6), .pin18(REG_IN7),
    .pin19(REG_OUT7), .pin20(1'b1));
  _7400 NAND_gate (
    .pin1(DS0_OUT), .pin2(DS1_OUT), .pin3(NAND_OUT), .pin4(1'b0), .pin5(1'b0), .pin7(1'b0), .pin9(1'b0),
    .pin10(1'b0), .pin12(1'b0), .pin13(1'b0), .pin14(1'b1));  // open: pin6, pin8, pin11
  _7432 OR_gate (
    .pin1(DS0_OUT), .pin2(DS1_OUT), .pin3(OR_OUT), .pin4(1'b0), .pin5(1'b0), .pin7(1'b0), .pin9(1'b0),
    .pin10(1'b0), .pin12(1'b0), .pin13(1'b0), .pin14(1'b1));  // open: pin6, pin8, pin11
  _74151 multiplexer0 (
    .pin1(DS3_OUT), .pin2(DS2_OUT), .pin3(DS1_OUT), .pin4(DS0_OUT), .pin5(MUX0_OUT), .pin7(1'b0),
    .pin8(1'b0), .pin9(MUXSEL_C), .pin10(MUXSEL_B), .pin11(MUXSEL_A), .pin12(in_2), .pin13(NAND_OUT),
    .pin14(ADDER_OUT), .pin15(DS0_OUT), .pin16(1'b1));  // open: pin6
  _74151 multiplexer1 (
    .pin1(XOR_OUT), .pin2(OR_OUT), .pin3(AND_OUT), .pin4(NOT_OUT), .pin5(MUX1_OUT), .pin7(1'b0), .pin8(1'b0),
    .pin9(MUXSEL_C), .pin10(MUXSEL_B), .pin11(MUXSEL_A), .pin12(1'b0), .pin13(DS0_OUT), .pin14(DS0_OUT),
    .pin15(DS0_OUT), .pin16(1'b1));  // open: pin6
  _7486 XOR_gate (
    .pin1(DS0_OUT), .pin2(DS1_OUT), .pin3(XOR_OUT), .pin4(1'b0), .pin5(1'b0), .pin7(1'b0), .pin9(1'b0),
    .pin10(1'b0), .pin12(1'b0), .pin13(1'b0), .pin14(1'b1));  // open: pin6, pin8, pin11
  _74157 multiplexer_select (
    .pin1(MUXSEL_D), .pin2(MUX0_OUT), .pin3(MUX1_OUT), .pin4(MUX_OUT), .pin5(1'b0), .pin6(1'b0), .pin8(1'b0),
    .pin10(1'b0), .pin11(1'b0), .pin13(1'b0), .pin14(1'b0), .pin15(1'b0), .pin16(1'b1));  // open: pin7, pin9, pin12
  _7404 NOT_gate (
    .pin1(DS0_OUT), .pin2(NOT_OUT), .pin3(1'b0), .pin5(1'b0), .pin7(1'b0), .pin9(1'b0), .pin11(1'b0),
    .pin13(1'b0), .pin14(1'b1));  // open: pin4, pin6, pin8, pin10, pin12
  _7474 _1_bit_stack_registers (
    .pin1(RESET), .pin2(DS0_IN), .pin3(clk), .pin4(1'b1), .pin5(DS0_OUT), .pin7(1'b0), .pin9(DS1_OUT),
    .pin10(1'b1), .pin11(clk), .pin12(DS1_IN), .pin13(RESET), .pin14(1'b1));  // open: pin6, pin8
  _7474 _1_bit_stack_registers_2 (
    .pin1(RESET), .pin2(DS2_IN), .pin3(clk), .pin4(1'b1), .pin5(DS2_OUT), .pin7(1'b0), .pin9(DS3_OUT),
    .pin10(1'b1), .pin11(clk), .pin12(DS3_IN), .pin13(RESET), .pin14(1'b1));  // open: pin6, pin8
  _74157 stack_direction_input_select (
    .pin1(STACKDIRSEL), .pin2(MUX_OUT), .pin3(DS1_OUT), .pin4(DS0_IN), .pin5(DS0_OUT), .pin6(DS2_OUT),
    .pin7(DS1_IN), .pin8(1'b0), .pin9(DS2_IN), .pin10(DS3_OUT), .pin11(DS1_OUT), .pin12(DS3_IN),
    .pin13(1'b0), .pin14(DS2_OUT), .pin15(1'b0), .pin16(1'b1));
  Counter #(.Bits(4)) counter_1 (.en(in_39), .C(clk_2), .clr(in_40), .out(counter_1_out));  // open: ovf
  not not_1 (not_1_out, in_28);
  not not_2 (not_2_out, counter_1_out[3]);
  _74238 _74238_1 (
    .pin1(in_25), .pin2(in_26), .pin3(in_27), .pin4(1'b0), .pin5(1'b0), .pin6(not_1_out), .pin7(out_16),
    .pin8(1'b0), .pin9(out_15), .pin10(out_14), .pin11(out_13), .pin12(out_12), .pin13(out_11),
    .pin14(out_10), .pin15(out_9), .pin16(1'b1));
  _74238 _74238_2 (
    .pin1(in_25), .pin2(in_26), .pin3(in_27), .pin4(1'b0), .pin5(1'b0), .pin6(in_28), .pin7(out_24),
    .pin8(1'b0), .pin9(out_23), .pin10(out_22), .pin11(out_21), .pin12(out_20), .pin13(out_19),
    .pin14(out_18), .pin15(out_17), .pin16(1'b1));
  _74238 _74238_3 (
    .pin1(counter_1_out[0]), .pin2(counter_1_out[1]), .pin3(counter_1_out[2]), .pin4(1'b0), .pin5(1'b0),
    .pin6(not_2_out), .pin7(out_8), .pin8(1'b0), .pin9(out_7), .pin10(out_29), .pin11(out_6), .pin12(out_37),
    .pin13(out_5), .pin14(out_4), .pin15(out_3), .pin16(1'b1));
  _74238 _74238_4 (
    .pin1(counter_1_out[0]), .pin2(counter_1_out[1]), .pin3(counter_1_out[2]), .pin4(1'b0), .pin5(1'b0),
    .pin6(counter_1_out[3]), .pin7(out_35), .pin8(1'b0), .pin9(out_38), .pin10(out_34), .pin11(out_33),
    .pin12(out_32), .pin13(out_31), .pin14(out_30), .pin15(out_36), .pin16(1'b1));
  PullDown pulldown_2 (.out(pulldown_2_out));
  assign pulldown_2_out = out_9 ? out_9 : 1'bz;  // Driver driver_1
  assign pulldown_2_out = out_10 ? out_10 : 1'bz;  // Driver driver_2
  assign pulldown_2_out = out_11 ? out_11 : 1'bz;  // Driver driver_3
  assign pulldown_2_out = out_12 ? out_12 : 1'bz;  // Driver driver_4
  assign pulldown_2_out = out_13 ? out_13 : 1'bz;  // Driver driver_5
  assign pulldown_2_out = out_14 ? out_14 : 1'bz;  // Driver driver_6
  assign pulldown_2_out = out_15 ? out_15 : 1'bz;  // Driver driver_7
  assign pulldown_2_out = out_16 ? out_16 : 1'bz;  // Driver driver_8
  assign pulldown_2_out = out_17 ? out_17 : 1'bz;  // Driver driver_9
  assign pulldown_2_out = out_18 ? out_18 : 1'bz;  // Driver driver_10
  assign pulldown_2_out = out_19 ? out_19 : 1'bz;  // Driver driver_11
  assign pulldown_2_out = out_20 ? out_20 : 1'bz;  // Driver driver_12
  assign pulldown_2_out = out_21 ? out_21 : 1'bz;  // Driver driver_13
  assign pulldown_2_out = out_22 ? out_22 : 1'bz;  // Driver driver_14
  assign pulldown_2_out = out_23 ? out_23 : 1'bz;  // Driver driver_15
  assign pulldown_2_out = out_24 ? out_24 : 1'bz;  // Driver driver_16
  LED led_7 (.in(pulldown_2_out));
  assign driver_17_out = out_9 ? out_9 : 1'bz;  // Driver driver_17
  assign driver_17_out = out_10 ? out_10 : 1'bz;  // Driver driver_18
  assign driver_17_out = out_11 ? out_11 : 1'bz;  // Driver driver_19
  assign driver_17_out = out_12 ? out_12 : 1'bz;  // Driver driver_20
  assign driver_17_out = out_13 ? out_13 : 1'bz;  // Driver driver_21
  assign driver_17_out = out_14 ? out_14 : 1'bz;  // Driver driver_22
  assign driver_17_out = out_15 ? out_15 : 1'bz;  // Driver driver_23
  assign driver_17_out = out_16 ? out_16 : 1'bz;  // Driver driver_24
  assign driver_17_out = out_17 ? out_17 : 1'bz;  // Driver driver_25
  assign driver_17_out = out_18 ? out_18 : 1'bz;  // Driver driver_26
  assign driver_17_out = out_19 ? out_19 : 1'bz;  // Driver driver_27
  assign driver_17_out = out_20 ? out_20 : 1'bz;  // Driver driver_28
  assign driver_17_out = out_21 ? out_21 : 1'bz;  // Driver driver_29
  assign driver_17_out = out_22 ? out_22 : 1'bz;  // Driver driver_30
  assign driver_17_out = out_23 ? out_23 : 1'bz;  // Driver driver_31
  assign driver_17_out = out_24 ? out_24 : 1'bz;  // Driver driver_32
  PullDown pulldown_3 (.out(driver_17_out));
  LED led_8 (.in(driver_17_out));
  PullDown pulldown_4 (.out(pulldown_4_out));
  assign pulldown_4_out = out_9 ? out_9 : 1'bz;  // Driver driver_33
  assign pulldown_4_out = out_10 ? out_10 : 1'bz;  // Driver driver_34
  assign pulldown_4_out = out_11 ? out_11 : 1'bz;  // Driver driver_35
  assign pulldown_4_out = out_12 ? out_12 : 1'bz;  // Driver driver_36
  assign pulldown_4_out = out_13 ? out_13 : 1'bz;  // Driver driver_37
  assign pulldown_4_out = out_14 ? out_14 : 1'bz;  // Driver driver_38
  assign pulldown_4_out = out_15 ? out_15 : 1'bz;  // Driver driver_39
  assign pulldown_4_out = out_16 ? out_16 : 1'bz;  // Driver driver_40
  assign pulldown_4_out = out_17 ? out_17 : 1'bz;  // Driver driver_41
  assign pulldown_4_out = out_18 ? out_18 : 1'bz;  // Driver driver_42
  assign pulldown_4_out = out_19 ? out_19 : 1'bz;  // Driver driver_43
  assign pulldown_4_out = out_20 ? out_20 : 1'bz;  // Driver driver_44
  assign pulldown_4_out = out_21 ? out_21 : 1'bz;  // Driver driver_45
  assign pulldown_4_out = out_22 ? out_22 : 1'bz;  // Driver driver_46
  assign pulldown_4_out = out_23 ? out_23 : 1'bz;  // Driver driver_47
  assign pulldown_4_out = out_24 ? out_24 : 1'bz;  // Driver driver_48
  LED led_9 (.in(pulldown_4_out));
  assign driver_49_out = out_9 ? out_9 : 1'bz;  // Driver driver_49
  assign driver_49_out = out_10 ? out_10 : 1'bz;  // Driver driver_50
  assign driver_49_out = out_11 ? out_11 : 1'bz;  // Driver driver_51
  assign driver_49_out = out_12 ? out_12 : 1'bz;  // Driver driver_52
  assign driver_49_out = out_13 ? out_13 : 1'bz;  // Driver driver_53
  assign driver_49_out = out_14 ? out_14 : 1'bz;  // Driver driver_54
  assign driver_49_out = out_15 ? out_15 : 1'bz;  // Driver driver_55
  assign driver_49_out = out_16 ? out_16 : 1'bz;  // Driver driver_56
  assign driver_49_out = out_17 ? out_17 : 1'bz;  // Driver driver_57
  assign driver_49_out = out_18 ? out_18 : 1'bz;  // Driver driver_58
  assign driver_49_out = out_19 ? out_19 : 1'bz;  // Driver driver_59
  assign driver_49_out = out_20 ? out_20 : 1'bz;  // Driver driver_60
  assign driver_49_out = out_21 ? out_21 : 1'bz;  // Driver driver_61
  assign driver_49_out = out_22 ? out_22 : 1'bz;  // Driver driver_62
  assign driver_49_out = out_23 ? out_23 : 1'bz;  // Driver driver_63
  assign driver_49_out = out_24 ? out_24 : 1'bz;  // Driver driver_64
  PullDown pulldown_5 (.out(pulldown_5_out));
  LED led_10 (.in(pulldown_5_out));
  PullDown pulldown_6 (.out(driver_49_out));
  LED led_11 (.in(driver_49_out));
  PullDown pulldown_7 (.out(pulldown_7_out));
  assign pulldown_7_out = out_38 ? out_38 : 1'bz;  // Driver driver_65
  assign pulldown_7_out = out_35 ? out_35 : 1'bz;  // Driver driver_66
  LED led_12 (.in(pulldown_7_out));
  assign driver_67_out = out_9 ? out_9 : 1'bz;  // Driver driver_67
  assign driver_67_out = out_10 ? out_10 : 1'bz;  // Driver driver_68
  assign driver_67_out = out_11 ? out_11 : 1'bz;  // Driver driver_69
  assign driver_67_out = out_12 ? out_12 : 1'bz;  // Driver driver_70
  assign driver_67_out = out_13 ? out_13 : 1'bz;  // Driver driver_71
  assign driver_67_out = out_14 ? out_14 : 1'bz;  // Driver driver_72
  assign driver_67_out = out_15 ? out_15 : 1'bz;  // Driver driver_73
  assign driver_67_out = out_16 ? out_16 : 1'bz;  // Driver driver_74
  assign driver_67_out = out_17 ? out_17 : 1'bz;  // Driver driver_75
  assign driver_67_out = out_18 ? out_18 : 1'bz;  // Driver driver_76
  assign driver_67_out = out_19 ? out_19 : 1'bz;  // Driver driver_77
  assign driver_67_out = out_20 ? out_20 : 1'bz;  // Driver driver_78
  assign driver_67_out = out_21 ? out_21 : 1'bz;  // Driver driver_79
  assign driver_67_out = out_22 ? out_22 : 1'bz;  // Driver driver_80
  assign driver_67_out = out_23 ? out_23 : 1'bz;  // Driver driver_81
  assign driver_67_out = out_24 ? out_24 : 1'bz;  // Driver driver_82
  assign driver_83_out = out_33 ? out_33 : 1'bz;  // Driver driver_83
  assign driver_83_out = out_34 ? out_34 : 1'bz;  // Driver driver_84
  PullDown pulldown_8 (.out(driver_67_out));
  LED led_13 (.in(driver_67_out));
  PullDown pulldown_9 (.out(driver_83_out));
  LED led_14 (.in(driver_83_out));
  PullDown pulldown_10 (.out(pulldown_10_out));
  assign pulldown_10_out = out_9 ? out_9 : 1'bz;  // Driver driver_85
  assign pulldown_10_out = out_10 ? out_10 : 1'bz;  // Driver driver_86
  assign pulldown_10_out = out_11 ? out_11 : 1'bz;  // Driver driver_87
  assign pulldown_10_out = out_12 ? out_12 : 1'bz;  // Driver driver_88
  assign pulldown_10_out = out_13 ? out_13 : 1'bz;  // Driver driver_89
  assign pulldown_10_out = out_14 ? out_14 : 1'bz;  // Driver driver_90
  assign pulldown_10_out = out_15 ? out_15 : 1'bz;  // Driver driver_91
  assign pulldown_10_out = out_16 ? out_16 : 1'bz;  // Driver driver_92
  assign pulldown_10_out = out_17 ? out_17 : 1'bz;  // Driver driver_93
  assign pulldown_10_out = out_18 ? out_18 : 1'bz;  // Driver driver_94
  assign pulldown_10_out = out_19 ? out_19 : 1'bz;  // Driver driver_95
  assign pulldown_10_out = out_20 ? out_20 : 1'bz;  // Driver driver_96
  assign pulldown_10_out = out_21 ? out_21 : 1'bz;  // Driver driver_97
  assign pulldown_10_out = out_22 ? out_22 : 1'bz;  // Driver driver_98
  assign pulldown_10_out = out_23 ? out_23 : 1'bz;  // Driver driver_99
  assign pulldown_10_out = out_24 ? out_24 : 1'bz;  // Driver driver_100
  LED led_15 (.in(pulldown_10_out));
  PullDown pulldown_11 (.out(pulldown_11_out));
  assign pulldown_11_out = out_32 ? out_32 : 1'bz;  // Driver driver_101
  LED led_16 (.in(pulldown_11_out));
  assign driver_102_out = out_9 ? out_9 : 1'bz;  // Driver driver_102
  assign driver_102_out = out_10 ? out_10 : 1'bz;  // Driver driver_103
  assign driver_102_out = out_11 ? out_11 : 1'bz;  // Driver driver_104
  assign driver_102_out = out_12 ? out_12 : 1'bz;  // Driver driver_105
  assign driver_102_out = out_13 ? out_13 : 1'bz;  // Driver driver_106
  assign driver_102_out = out_14 ? out_14 : 1'bz;  // Driver driver_107
  assign driver_102_out = out_15 ? out_15 : 1'bz;  // Driver driver_108
  assign driver_102_out = out_16 ? out_16 : 1'bz;  // Driver driver_109
  assign driver_102_out = out_17 ? out_17 : 1'bz;  // Driver driver_110
  assign driver_102_out = out_18 ? out_18 : 1'bz;  // Driver driver_111
  assign driver_102_out = out_19 ? out_19 : 1'bz;  // Driver driver_112
  assign driver_102_out = out_20 ? out_20 : 1'bz;  // Driver driver_113
  assign driver_102_out = out_21 ? out_21 : 1'bz;  // Driver driver_114
  assign driver_102_out = out_22 ? out_22 : 1'bz;  // Driver driver_115
  assign driver_102_out = out_23 ? out_23 : 1'bz;  // Driver driver_116
  assign driver_102_out = out_24 ? out_24 : 1'bz;  // Driver driver_117
  assign driver_118_out = out_31 ? out_31 : 1'bz;  // Driver driver_118
  PullDown pulldown_12 (.out(driver_102_out));
  LED led_17 (.in(driver_102_out));
  PullDown pulldown_13 (.out(driver_118_out));
  LED led_18 (.in(driver_118_out));
  PullDown pulldown_14 (.out(pulldown_14_out));
  assign pulldown_14_out = out_9 ? out_9 : 1'bz;  // Driver driver_119
  assign pulldown_14_out = out_10 ? out_10 : 1'bz;  // Driver driver_120
  assign pulldown_14_out = out_11 ? out_11 : 1'bz;  // Driver driver_121
  assign pulldown_14_out = out_12 ? out_12 : 1'bz;  // Driver driver_122
  assign pulldown_14_out = out_13 ? out_13 : 1'bz;  // Driver driver_123
  assign pulldown_14_out = out_14 ? out_14 : 1'bz;  // Driver driver_124
  assign pulldown_14_out = out_15 ? out_15 : 1'bz;  // Driver driver_125
  assign pulldown_14_out = out_16 ? out_16 : 1'bz;  // Driver driver_126
  assign pulldown_14_out = out_17 ? out_17 : 1'bz;  // Driver driver_127
  assign pulldown_14_out = out_18 ? out_18 : 1'bz;  // Driver driver_128
  assign pulldown_14_out = out_19 ? out_19 : 1'bz;  // Driver driver_129
  assign pulldown_14_out = out_20 ? out_20 : 1'bz;  // Driver driver_130
  assign pulldown_14_out = out_21 ? out_21 : 1'bz;  // Driver driver_131
  assign pulldown_14_out = out_22 ? out_22 : 1'bz;  // Driver driver_132
  assign pulldown_14_out = out_23 ? out_23 : 1'bz;  // Driver driver_133
  assign pulldown_14_out = out_24 ? out_24 : 1'bz;  // Driver driver_134
  LED led_19 (.in(pulldown_14_out));
  PullDown pulldown_15 (.out(pulldown_15_out));
  assign pulldown_15_out = out_30 ? out_30 : 1'bz;  // Driver driver_135
  LED led_20 (.in(pulldown_15_out));
  assign driver_136_out = out_9 ? out_9 : 1'bz;  // Driver driver_136
  assign driver_136_out = out_10 ? out_10 : 1'bz;  // Driver driver_137
  assign driver_136_out = out_11 ? out_11 : 1'bz;  // Driver driver_138
  assign driver_136_out = out_12 ? out_12 : 1'bz;  // Driver driver_139
  assign driver_136_out = out_13 ? out_13 : 1'bz;  // Driver driver_140
  assign driver_136_out = out_14 ? out_14 : 1'bz;  // Driver driver_141
  assign driver_136_out = out_15 ? out_15 : 1'bz;  // Driver driver_142
  assign driver_136_out = out_16 ? out_16 : 1'bz;  // Driver driver_143
  assign driver_136_out = out_17 ? out_17 : 1'bz;  // Driver driver_144
  assign driver_136_out = out_18 ? out_18 : 1'bz;  // Driver driver_145
  assign driver_136_out = out_19 ? out_19 : 1'bz;  // Driver driver_146
  assign driver_136_out = out_20 ? out_20 : 1'bz;  // Driver driver_147
  assign driver_136_out = out_21 ? out_21 : 1'bz;  // Driver driver_148
  assign driver_136_out = out_22 ? out_22 : 1'bz;  // Driver driver_149
  assign driver_136_out = out_23 ? out_23 : 1'bz;  // Driver driver_150
  assign driver_136_out = out_24 ? out_24 : 1'bz;  // Driver driver_151
  assign driver_152_out = out_36 ? out_36 : 1'bz;  // Driver driver_152
  PullDown pulldown_16 (.out(driver_136_out));
  LED led_21 (.in(driver_136_out));
  PullDown pulldown_17 (.out(driver_152_out));
  LED led_22 (.in(driver_152_out));
  PullDown pulldown_18 (.out(pulldown_18_out));
  assign pulldown_18_out = out_9 ? out_9 : 1'bz;  // Driver driver_153
  assign pulldown_18_out = out_10 ? out_10 : 1'bz;  // Driver driver_154
  assign pulldown_18_out = out_11 ? out_11 : 1'bz;  // Driver driver_155
  assign pulldown_18_out = out_12 ? out_12 : 1'bz;  // Driver driver_156
  assign pulldown_18_out = out_13 ? out_13 : 1'bz;  // Driver driver_157
  assign pulldown_18_out = out_14 ? out_14 : 1'bz;  // Driver driver_158
  assign pulldown_18_out = out_15 ? out_15 : 1'bz;  // Driver driver_159
  assign pulldown_18_out = out_16 ? out_16 : 1'bz;  // Driver driver_160
  assign pulldown_18_out = out_17 ? out_17 : 1'bz;  // Driver driver_161
  assign pulldown_18_out = out_18 ? out_18 : 1'bz;  // Driver driver_162
  assign pulldown_18_out = out_19 ? out_19 : 1'bz;  // Driver driver_163
  assign pulldown_18_out = out_20 ? out_20 : 1'bz;  // Driver driver_164
  assign pulldown_18_out = out_21 ? out_21 : 1'bz;  // Driver driver_165
  assign pulldown_18_out = out_22 ? out_22 : 1'bz;  // Driver driver_166
  assign pulldown_18_out = out_23 ? out_23 : 1'bz;  // Driver driver_167
  assign pulldown_18_out = out_24 ? out_24 : 1'bz;  // Driver driver_168
  LED led_23 (.in(pulldown_18_out));
  PullDown pulldown_19 (.out(pulldown_19_out));
  assign pulldown_19_out = out_7 ? out_7 : 1'bz;  // Driver driver_169
  assign pulldown_19_out = out_8 ? out_8 : 1'bz;  // Driver driver_170
  LED led_24 (.in(pulldown_19_out));
  assign driver_171_out = out_9 ? out_9 : 1'bz;  // Driver driver_171
  assign driver_171_out = out_10 ? out_10 : 1'bz;  // Driver driver_172
  assign driver_171_out = out_11 ? out_11 : 1'bz;  // Driver driver_173
  assign driver_171_out = out_12 ? out_12 : 1'bz;  // Driver driver_174
  assign driver_171_out = out_13 ? out_13 : 1'bz;  // Driver driver_175
  assign driver_171_out = out_14 ? out_14 : 1'bz;  // Driver driver_176
  assign driver_171_out = out_15 ? out_15 : 1'bz;  // Driver driver_177
  assign driver_171_out = out_16 ? out_16 : 1'bz;  // Driver driver_178
  assign driver_171_out = out_17 ? out_17 : 1'bz;  // Driver driver_179
  assign driver_171_out = out_18 ? out_18 : 1'bz;  // Driver driver_180
  assign driver_171_out = out_19 ? out_19 : 1'bz;  // Driver driver_181
  assign driver_171_out = out_20 ? out_20 : 1'bz;  // Driver driver_182
  assign driver_171_out = out_21 ? out_21 : 1'bz;  // Driver driver_183
  assign driver_171_out = out_22 ? out_22 : 1'bz;  // Driver driver_184
  assign driver_171_out = out_23 ? out_23 : 1'bz;  // Driver driver_185
  assign driver_171_out = out_24 ? out_24 : 1'bz;  // Driver driver_186
  assign driver_187_out = out_6 ? out_6 : 1'bz;  // Driver driver_187
  assign driver_187_out = out_29 ? out_29 : 1'bz;  // Driver driver_188
  PullDown pulldown_20 (.out(driver_171_out));
  LED led_25 (.in(driver_171_out));
  PullDown pulldown_21 (.out(driver_187_out));
  LED led_26 (.in(driver_187_out));
  PullDown pulldown_22 (.out(pulldown_22_out));
  assign pulldown_22_out = out_9 ? out_9 : 1'bz;  // Driver driver_189
  assign pulldown_22_out = out_10 ? out_10 : 1'bz;  // Driver driver_190
  assign pulldown_22_out = out_11 ? out_11 : 1'bz;  // Driver driver_191
  assign pulldown_22_out = out_12 ? out_12 : 1'bz;  // Driver driver_192
  assign pulldown_22_out = out_13 ? out_13 : 1'bz;  // Driver driver_193
  assign pulldown_22_out = out_14 ? out_14 : 1'bz;  // Driver driver_194
  assign pulldown_22_out = out_15 ? out_15 : 1'bz;  // Driver driver_195
  assign pulldown_22_out = out_16 ? out_16 : 1'bz;  // Driver driver_196
  assign pulldown_22_out = out_17 ? out_17 : 1'bz;  // Driver driver_197
  assign pulldown_22_out = out_18 ? out_18 : 1'bz;  // Driver driver_198
  assign pulldown_22_out = out_19 ? out_19 : 1'bz;  // Driver driver_199
  assign pulldown_22_out = out_20 ? out_20 : 1'bz;  // Driver driver_200
  assign pulldown_22_out = out_21 ? out_21 : 1'bz;  // Driver driver_201
  assign pulldown_22_out = out_22 ? out_22 : 1'bz;  // Driver driver_202
  assign pulldown_22_out = out_23 ? out_23 : 1'bz;  // Driver driver_203
  assign pulldown_22_out = out_24 ? out_24 : 1'bz;  // Driver driver_204
  LED led_27 (.in(pulldown_22_out));
  PullDown pulldown_23 (.out(pulldown_23_out));
  assign pulldown_23_out = out_4 ? out_4 : 1'bz;  // Driver driver_205
  assign pulldown_23_out = out_5 ? out_5 : 1'bz;  // Driver driver_206
  assign pulldown_23_out = out_37 ? out_37 : 1'bz;  // Driver driver_207
  LED led_28 (.in(pulldown_23_out));
  assign driver_208_out = out_3 ? out_3 : 1'bz;  // Driver driver_208
  PullDown pulldown_24 (.out(pulldown_24_out));
  assign pulldown_24_out = out_9 ? out_9 : 1'bz;  // Driver driver_209
  assign pulldown_24_out = out_10 ? out_10 : 1'bz;  // Driver driver_210
  assign pulldown_24_out = out_11 ? out_11 : 1'bz;  // Driver driver_211
  assign pulldown_24_out = out_12 ? out_12 : 1'bz;  // Driver driver_212
  assign pulldown_24_out = out_13 ? out_13 : 1'bz;  // Driver driver_213
  assign pulldown_24_out = out_14 ? out_14 : 1'bz;  // Driver driver_214
  assign pulldown_24_out = out_15 ? out_15 : 1'bz;  // Driver driver_215
  assign pulldown_24_out = out_16 ? out_16 : 1'bz;  // Driver driver_216
  assign pulldown_24_out = out_17 ? out_17 : 1'bz;  // Driver driver_217
  assign pulldown_24_out = out_18 ? out_18 : 1'bz;  // Driver driver_218
  assign pulldown_24_out = out_19 ? out_19 : 1'bz;  // Driver driver_219
  assign pulldown_24_out = out_20 ? out_20 : 1'bz;  // Driver driver_220
  assign pulldown_24_out = out_21 ? out_21 : 1'bz;  // Driver driver_221
  assign pulldown_24_out = out_22 ? out_22 : 1'bz;  // Driver driver_222
  assign pulldown_24_out = out_23 ? out_23 : 1'bz;  // Driver driver_223
  assign pulldown_24_out = out_24 ? out_24 : 1'bz;  // Driver driver_224
  LED led_29 (.in(pulldown_24_out));
  PullDown pulldown_25 (.out(driver_208_out));
  LED led_30 (.in(driver_208_out));
  assign driver_225_out = out_9 ? out_9 : 1'bz;  // Driver driver_225
  assign driver_225_out = out_10 ? out_10 : 1'bz;  // Driver driver_226
  assign driver_225_out = out_11 ? out_11 : 1'bz;  // Driver driver_227
  assign driver_225_out = out_12 ? out_12 : 1'bz;  // Driver driver_228
  assign driver_225_out = out_13 ? out_13 : 1'bz;  // Driver driver_229
  assign driver_225_out = out_14 ? out_14 : 1'bz;  // Driver driver_230
  assign driver_225_out = out_15 ? out_15 : 1'bz;  // Driver driver_231
  assign driver_225_out = out_16 ? out_16 : 1'bz;  // Driver driver_232
  assign driver_225_out = out_17 ? out_17 : 1'bz;  // Driver driver_233
  assign driver_225_out = out_18 ? out_18 : 1'bz;  // Driver driver_234
  assign driver_225_out = out_19 ? out_19 : 1'bz;  // Driver driver_235
  assign driver_225_out = out_20 ? out_20 : 1'bz;  // Driver driver_236
  assign driver_225_out = out_21 ? out_21 : 1'bz;  // Driver driver_237
  assign driver_225_out = out_22 ? out_22 : 1'bz;  // Driver driver_238
  assign driver_225_out = out_23 ? out_23 : 1'bz;  // Driver driver_239
  assign driver_225_out = out_24 ? out_24 : 1'bz;  // Driver driver_240
  PullDown pulldown_26 (.out(pulldown_26_out));
  assign pulldown_26_out = out_3 ? out_3 : 1'bz;  // Driver driver_241
  assign pulldown_26_out = out_5 ? out_5 : 1'bz;  // Driver driver_242
  assign pulldown_26_out = out_37 ? out_37 : 1'bz;  // Driver driver_243
  assign pulldown_26_out = out_29 ? out_29 : 1'bz;  // Driver driver_244
  assign pulldown_26_out = out_8 ? out_8 : 1'bz;  // Driver driver_245
  assign pulldown_26_out = out_30 ? out_30 : 1'bz;  // Driver driver_246
  assign pulldown_26_out = out_31 ? out_31 : 1'bz;  // Driver driver_247
  assign pulldown_26_out = out_32 ? out_32 : 1'bz;  // Driver driver_248
  assign pulldown_26_out = out_33 ? out_33 : 1'bz;  // Driver driver_249
  assign pulldown_26_out = out_34 ? out_34 : 1'bz;  // Driver driver_250
  assign pulldown_26_out = out_38 ? out_38 : 1'bz;  // Driver driver_251
  assign pulldown_26_out = out_35 ? out_35 : 1'bz;  // Driver driver_252
  LED led_31 (.in(pulldown_26_out));
  PullDown pulldown_27 (.out(driver_225_out));
  LED led_32 (.in(driver_225_out));
  assign driver_253_out = out_3 ? out_3 : 1'bz;  // Driver driver_253
  assign driver_253_out = out_5 ? out_5 : 1'bz;  // Driver driver_254
  assign driver_253_out = out_37 ? out_37 : 1'bz;  // Driver driver_255
  assign driver_253_out = out_29 ? out_29 : 1'bz;  // Driver driver_256
  assign driver_253_out = out_7 ? out_7 : 1'bz;  // Driver driver_257
  assign driver_253_out = out_8 ? out_8 : 1'bz;  // Driver driver_258
  assign driver_253_out = out_30 ? out_30 : 1'bz;  // Driver driver_259
  assign driver_253_out = out_31 ? out_31 : 1'bz;  // Driver driver_260
  assign driver_253_out = out_32 ? out_32 : 1'bz;  // Driver driver_261
  assign driver_253_out = out_33 ? out_33 : 1'bz;  // Driver driver_262
  assign driver_253_out = out_34 ? out_34 : 1'bz;  // Driver driver_263
  assign driver_253_out = out_38 ? out_38 : 1'bz;  // Driver driver_264
  assign driver_253_out = out_35 ? out_35 : 1'bz;  // Driver driver_265
  PullDown pulldown_28 (.out(pulldown_28_out));
  assign pulldown_28_out = out_9 ? out_9 : 1'bz;  // Driver driver_266
  assign pulldown_28_out = out_10 ? out_10 : 1'bz;  // Driver driver_267
  assign pulldown_28_out = out_11 ? out_11 : 1'bz;  // Driver driver_268
  assign pulldown_28_out = out_12 ? out_12 : 1'bz;  // Driver driver_269
  assign pulldown_28_out = out_13 ? out_13 : 1'bz;  // Driver driver_270
  assign pulldown_28_out = out_14 ? out_14 : 1'bz;  // Driver driver_271
  assign pulldown_28_out = out_15 ? out_15 : 1'bz;  // Driver driver_272
  assign pulldown_28_out = out_16 ? out_16 : 1'bz;  // Driver driver_273
  assign pulldown_28_out = out_17 ? out_17 : 1'bz;  // Driver driver_274
  assign pulldown_28_out = out_18 ? out_18 : 1'bz;  // Driver driver_275
  assign pulldown_28_out = out_19 ? out_19 : 1'bz;  // Driver driver_276
  assign pulldown_28_out = out_20 ? out_20 : 1'bz;  // Driver driver_277
  assign pulldown_28_out = out_21 ? out_21 : 1'bz;  // Driver driver_278
  assign pulldown_28_out = out_22 ? out_22 : 1'bz;  // Driver driver_279
  assign pulldown_28_out = out_23 ? out_23 : 1'bz;  // Driver driver_280
  assign pulldown_28_out = out_24 ? out_24 : 1'bz;  // Driver driver_281
  LED led_33 (.in(pulldown_28_out));
  PullDown pulldown_29 (.out(driver_253_out));
  LED led_34 (.in(driver_253_out));
  assign driver_282_out = out_9 ? out_9 : 1'bz;  // Driver driver_282
  assign driver_282_out = out_10 ? out_10 : 1'bz;  // Driver driver_283
  assign driver_282_out = out_11 ? out_11 : 1'bz;  // Driver driver_284
  assign driver_282_out = out_12 ? out_12 : 1'bz;  // Driver driver_285
  assign driver_282_out = out_13 ? out_13 : 1'bz;  // Driver driver_286
  assign driver_282_out = out_14 ? out_14 : 1'bz;  // Driver driver_287
  assign driver_282_out = out_15 ? out_15 : 1'bz;  // Driver driver_288
  assign driver_282_out = out_16 ? out_16 : 1'bz;  // Driver driver_289
  assign driver_282_out = out_17 ? out_17 : 1'bz;  // Driver driver_290
  assign driver_282_out = out_18 ? out_18 : 1'bz;  // Driver driver_291
  assign driver_282_out = out_19 ? out_19 : 1'bz;  // Driver driver_292
  assign driver_282_out = out_20 ? out_20 : 1'bz;  // Driver driver_293
  assign driver_282_out = out_21 ? out_21 : 1'bz;  // Driver driver_294
  assign driver_282_out = out_22 ? out_22 : 1'bz;  // Driver driver_295
  assign driver_282_out = out_23 ? out_23 : 1'bz;  // Driver driver_296
  assign driver_282_out = out_24 ? out_24 : 1'bz;  // Driver driver_297
  PullDown pulldown_30 (.out(pulldown_30_out));
  assign pulldown_30_out = out_3 ? out_3 : 1'bz;  // Driver driver_298
  assign pulldown_30_out = out_5 ? out_5 : 1'bz;  // Driver driver_299
  assign pulldown_30_out = out_37 ? out_37 : 1'bz;  // Driver driver_300
  assign pulldown_30_out = out_6 ? out_6 : 1'bz;  // Driver driver_301
  assign pulldown_30_out = out_29 ? out_29 : 1'bz;  // Driver driver_302
  assign pulldown_30_out = out_7 ? out_7 : 1'bz;  // Driver driver_303
  assign pulldown_30_out = out_8 ? out_8 : 1'bz;  // Driver driver_304
  assign pulldown_30_out = out_30 ? out_30 : 1'bz;  // Driver driver_305
  assign pulldown_30_out = out_31 ? out_31 : 1'bz;  // Driver driver_306
  assign pulldown_30_out = out_32 ? out_32 : 1'bz;  // Driver driver_307
  assign pulldown_30_out = out_33 ? out_33 : 1'bz;  // Driver driver_308
  assign pulldown_30_out = out_34 ? out_34 : 1'bz;  // Driver driver_309
  assign pulldown_30_out = out_38 ? out_38 : 1'bz;  // Driver driver_310
  assign pulldown_30_out = out_35 ? out_35 : 1'bz;  // Driver driver_311
  LED led_35 (.in(pulldown_30_out));
  PullDown pulldown_31 (.out(driver_282_out));
  LED led_36 (.in(driver_282_out));
  assign driver_312_out = out_3 ? out_3 : 1'bz;  // Driver driver_312
  assign driver_312_out = out_4 ? out_4 : 1'bz;  // Driver driver_313
  assign driver_312_out = out_5 ? out_5 : 1'bz;  // Driver driver_314
  assign driver_312_out = out_37 ? out_37 : 1'bz;  // Driver driver_315
  assign driver_312_out = out_6 ? out_6 : 1'bz;  // Driver driver_316
  assign driver_312_out = out_29 ? out_29 : 1'bz;  // Driver driver_317
  assign driver_312_out = out_7 ? out_7 : 1'bz;  // Driver driver_318
  assign driver_312_out = out_8 ? out_8 : 1'bz;  // Driver driver_319
  assign driver_312_out = out_30 ? out_30 : 1'bz;  // Driver driver_320
  assign driver_312_out = out_31 ? out_31 : 1'bz;  // Driver driver_321
  assign driver_312_out = out_32 ? out_32 : 1'bz;  // Driver driver_322
  assign driver_312_out = out_33 ? out_33 : 1'bz;  // Driver driver_323
  assign driver_312_out = out_34 ? out_34 : 1'bz;  // Driver driver_324
  assign driver_312_out = out_38 ? out_38 : 1'bz;  // Driver driver_325
  assign driver_312_out = out_35 ? out_35 : 1'bz;  // Driver driver_326
  PullDown pulldown_32 (.out(driver_312_out));
  LED led_37 (.in(driver_312_out));
  PullDown pulldown_33 (.out(pulldown_33_out));
  assign pulldown_33_out = out_37 ? out_37 : 1'bz;  // Driver driver_327
  assign pulldown_33_out = out_30 ? out_30 : 1'bz;  // Driver driver_328
  assign pulldown_33_out = out_31 ? out_31 : 1'bz;  // Driver driver_329
  assign pulldown_33_out = out_34 ? out_34 : 1'bz;  // Driver driver_330
  assign pulldown_33_out = out_35 ? out_35 : 1'bz;  // Driver driver_331

  // Other names for the same wires on the sheet: CLK_DS0 = clk; CLK_DS1 = clk; CLK_DS2 = clk; CLK_DS3 = clk;
  //   DATABUS = in_2; LEFTBIT_0 = DS0_OUT; LEFTBIT_LSB = DS0_OUT; RIGHTBIT_0 = DS0_OUT; RIGHTBIT_MSB = DS0_OUT

  // Notes on the sheet:
  //   contents of eeprom_1 (hex, n*v repeats v):
  //   0,1,a,3
  //   Clock
  //   Logic
  //   Instruction Register
  //   Connected due to 1-bit
  //   Plexing
  //   Data Stack
  //   15
  //   14
  //   13
  //   INPUT2
  //   12
  //   INPUT1
  //   11
  //   DATABUS
  //   10
  //   NAND
  //   9
  //   ADDER
  //   8
  //   LEFTBIT_LSB
  //   7
  //   DS3
  //   6
  //   DS2
  //   5
  //   DS1
  //   4
  //   DS0
  //   3
  //   DS4_EN
  //   2
  //   DS3_EN
  //   1
  //   DS2_EN
  //   0
  //   DS1_EN
  //   STACK DIRECTION
  //   DUP
  //   SWAP
  //   OVER
  //   POP
  //   ROT
  //   UNNAMMED
  //   2SWAP
  //   2OVER
  //   ROTATE-1-RIGHT
  //   ADD
  //   PUSH
  //   INPUT1_DOWN
  //   INPUT1_UP
  //   INPUT2_DOWN
  //   INPUT2_UP
endmodule
