// Digital circuit bit-slice.dig as structural Verilog
module bit_slice (
  input  DATA_BUS,
  input  LEFT_BIT,
  input  RIGHT_BIT,
  input  in_4
);

  wire and_4_out, and_5_out, and_6_out, and_7_out, and_8_out, and_9_out, and_10_out, and_11_out, and_12_out,
       button_2_out, CLK, CLK_A, CLK_B, CLK_S, CLKA_EN, CLKB_EN, CLKS_EN, d_ff_3_q, d_ff_4_q, DATASOURCE,
       DIR_DS0, DIR_DS1, DIR_S, DS0, DS1, nand_1_out, not_1_out, not_2_out, not_3_out, not_4_out, or_1_out,
       or_2_out, or_3_out, or_4_out, pulldown_1_out, xor_1_out;
  wire [3:0] dipswitch_4_out;
  wire [7:0] CLKA_EN_out;
  wire [7:6] register_1_q;

  Button button_1 (.out(CLK));
  and and_1 (CLK_A, CLK, CLKA_EN);
  and and_2 (CLK_B, CLK, CLKB_EN);
  and and_3 (CLK_S, CLK, CLKS_EN);
  DipSwitch u_CLKA_EN (.out(CLKA_EN_out[0]));
  DipSwitch u_CLKB_EN (.out(CLKA_EN_out[1]));
  DipSwitch u_CLKS_EN (.out(CLKA_EN_out[2]));
  DipSwitch DIRA (.out(CLKA_EN_out[3]));
  DipSwitch DIRB (.out(CLKA_EN_out[4]));
  DipSwitch DIRS (.out(CLKA_EN_out[5]));
  DipSwitch dipswitch_1 (.out(CLKA_EN_out[6]));
  DipSwitch dipswitch_2 (.out(CLKA_EN_out[7]));
  Register #(.Bits(8)) register_1 (
    .D(CLKA_EN_out), .C(button_2_out), .en(in_4),
    .Q({register_1_q, DIR_S, DIR_DS1, DIR_DS0, CLKS_EN, CLKB_EN, CLKA_EN}));
  Button button_2 (.out(button_2_out));
  not not_1 (not_1_out, DIR_DS0);
  not not_2 (not_2_out, DIR_DS1);
  not not_3 (not_3_out, DIR_S);
  DipSwitch dipswitch_3 (.out(dipswitch_4_out[2]));
  DipSwitch dipswitch_4 (.out(dipswitch_4_out[3]));
  and and_4 (and_4_out, DS0, DS1);
  nand nand_1 (nand_1_out, DS0, DS1);
  xor xor_1 (xor_1_out, DS0, DS1);
  PullDown pulldown_1 (.out(pulldown_1_out));
  DipSwitch dipswitch_5 (.out(dipswitch_4_out[0]));
  DipSwitch dipswitch_6 (.out(dipswitch_4_out[1]));
  not not_4 (not_4_out, DS0);
  and and_5 (and_5_out, DATASOURCE, not_1_out);
  and and_6 (and_6_out, DIR_DS0, DS1);
  and and_7 (and_7_out, DS0, not_2_out);
  and and_8 (and_8_out, DIR_DS1, d_ff_3_q);
  and and_9 (and_9_out, DS1, not_3_out);
  and and_10 (and_10_out, DIR_S, d_ff_4_q);
  and and_11 (and_11_out, d_ff_3_q, not_3_out);
  and and_12 (and_12_out, DIR_S, pulldown_1_out);
  or or_1 (or_1_out, and_5_out, and_6_out);
  or or_2 (or_2_out, and_7_out, and_8_out);
  or or_3 (or_3_out, and_9_out, and_10_out);
  or or_4 (or_4_out, and_11_out, and_12_out);
  Multiplexer #(.Selector_Bits(4)) multiplexer_1 (
    .sel(dipswitch_4_out), .in_0(DATA_BUS), .in_1(LEFT_BIT), .in_2(RIGHT_BIT), .in_3(1'b0), .in_4(1'b0),
    .in_5(1'b0), .in_6(1'b0), .in_7(1'b0), .in_8(1'b0), .in_9(1'b0), .in_10(DS0), .in_11(not_4_out),
    .in_12(and_4_out), .in_13(nand_1_out), .in_14(xor_1_out), .in_15(DS1), .out(DATASOURCE));
  D_FF d_ff_1 (.D(or_1_out), .C(CLK_A), .Q(DS0));  // open: nQ
  D_FF d_ff_2 (.D(or_2_out), .C(CLK_B), .Q(DS1));  // open: nQ
  D_FF d_ff_3 (.D(or_3_out), .C(CLK_S), .Q(d_ff_3_q));  // open: nQ
  D_FF d_ff_4 (.D(or_4_out), .C(CLK_S), .Q(d_ff_4_q));  // open: nQ
  LED led_1 (.in(DS0));
  LED led_2 (.in(DS1));
  LED led_3 (.in(d_ff_3_q));
  LED led_4 (.in(d_ff_4_q));

  // Notes on the sheet:
  //   in_4: default 1
  //   Possible OP Codes
  //   -----------------------------
  //   0000 NOP
  //   0001 PUSH
  //   0010 OVER
  //   0011 DUP
  //   0100 SWAP
  //   0101 POP
  //   0110 DROP
  //   0111
  //   1000 INVERT
  //   1001 AND
  //   1010 NAND
  //   1011 OR
  //   1100 NOR
  //   1101 XOR
  //   1110 XNOR
  //   1111
  //   LEFT BIT
  //   RIGHT BIT
endmodule

/* Code that sets the parameters or builds the circuit:
______DIR0 DIR1 DIR2   CLK0 CLK1 CLK2   SRC   OUT
PUSH   0    0    0      1    1    1     DATA  0
OVER   0    0    0      1    1    1     DS1   0
DUP    0    0    0      1    1    1     DS0   0
SWAP   0    0    -      1    1    0     DS1   0

POP    1    1    1      1    1    1      -    1
DROP   1    1    1      1    1    1      -    0

DIR: 1-bit
CLK: always on
CLK OUT EN: 1-bit
SRC: 3-bit
OUT EN: 1-bit
*/
