// Digital circuit stack module ttl.dig as structural Verilog
module stack_module_ttl (
  input  A,
  input  B,
  input  C,
  input  IN0,
  input  IN1,
  input  IN2,
  input  IN3,
  input  DS4,
  input  DS0_EN,
  input  DS1_EN,
  input  DS2_EN,
  input  DS3_EN,
  input  CLOCK,
  input  DIR,
  output out_13,
  output out_14,
  output out_15,
  output out_16
);

  wire _7408_1_pin3, _7408_1_pin6, _7474_1_pin2, _7474_1_pin3, _7474_1_pin11, _7474_1_pin12, _7474_2_pin2,
       _7474_2_pin12;

  _7474 _7474_1 (
    .pin1(1'b1), .pin2(_7474_1_pin2), .pin3(_7474_1_pin3), .pin4(1'b1), .pin5(out_13), .pin7(1'b0),
    .pin9(out_14), .pin10(1'b1), .pin11(_7474_1_pin11), .pin12(_7474_1_pin12), .pin13(1'b1), .pin14(1'b1));  // open: pin6, pin8
  _74151 _74151_1 (
    .pin1(out_16), .pin2(out_15), .pin3(out_14), .pin4(out_13), .pin5(_7474_1_pin2), .pin7(1'b0),
    .pin8(1'b0), .pin9(C), .pin10(B), .pin11(A), .pin12(IN3), .pin13(IN2), .pin14(IN1), .pin15(IN0),
    .pin16(1'b1));  // open: pin6
  _7408 _7408_1 (
    .pin1(DS3_EN), .pin2(CLOCK), .pin3(_7408_1_pin3), .pin4(DS2_EN), .pin5(CLOCK), .pin6(_7408_1_pin6),
    .pin7(1'b0), .pin8(_7474_1_pin11), .pin9(DS1_EN), .pin10(CLOCK), .pin11(_7474_1_pin3), .pin12(DS0_EN),
    .pin13(CLOCK), .pin14(1'b1));
  _7474 _7474_2 (
    .pin1(1'b1), .pin2(_7474_2_pin2), .pin3(_7408_1_pin6), .pin4(1'b1), .pin5(out_15), .pin7(1'b0),
    .pin9(out_16), .pin10(1'b1), .pin11(_7408_1_pin3), .pin12(_7474_2_pin12), .pin13(1'b1), .pin14(1'b1));  // open: pin6, pin8
  _74157 _74157_1 (
    .pin1(DIR), .pin2(out_13), .pin3(out_15), .pin4(_7474_1_pin12), .pin5(out_14), .pin6(out_16),
    .pin7(_7474_2_pin2), .pin8(1'b0), .pin9(_7474_2_pin12), .pin10(DS4), .pin11(out_15), .pin13(1'b0),
    .pin14(1'b0), .pin15(1'b0), .pin16(1'b1));  // open: pin12

  // Other names for the same wires on the sheet: DIRECTION = DIR; DS0 = out_13; DS1 = out_14; DS2 = out_15;
  //   DS3 = out_16
endmodule
