// Digital circuit stack module.dig as structural Verilog
module stack_module (
  input  IN0,
  input  IN1,
  input  IN2,
  input  IN3,
  input  A,
  input  B,
  input  C,
  input  CLOCK,
  input  DS0_EN,
  input  DS1_EN,
  input  DS2_EN,
  input  DS3_EN,
  input  DS4,
  input  DIR,
  output DS3,
  output DS2,
  output DS1,
  output DS0
);

  wire and_1_out, and_2_out, and_3_out, and_4_out, multiplexer_1_out, multiplexer_2_out, multiplexer_3_out,
       multiplexer_4_out;

  and and_1 (and_1_out, CLOCK, DS0_EN);
  and and_2 (and_2_out, CLOCK, DS1_EN);
  and and_3 (and_3_out, CLOCK, DS2_EN);
  and and_4 (and_4_out, CLOCK, DS3_EN);
  Multiplexer #(.Selector_Bits(3)) multiplexer_1 (
    .sel({C, B, A}), .in_0(DS0), .in_1(DS1), .in_2(DS2), .in_3(DS3), .in_4(IN0), .in_5(IN1), .in_6(IN2),
    .in_7(IN3), .out(multiplexer_1_out));
  Multiplexer multiplexer_2 (.sel(DIR), .in_0(DS0), .in_1(DS2), .out(multiplexer_2_out));
  Multiplexer multiplexer_3 (.sel(DIR), .in_0(DS1), .in_1(DS3), .out(multiplexer_3_out));
  Multiplexer multiplexer_4 (.sel(DIR), .in_0(DS2), .in_1(DS4), .out(multiplexer_4_out));
  D_FF d_ff_1 (.D(multiplexer_1_out), .C(and_1_out), .Q(DS0));  // open: nQ
  D_FF d_ff_2 (.D(multiplexer_2_out), .C(and_2_out), .Q(DS1));  // open: nQ
  D_FF d_ff_3 (.D(multiplexer_3_out), .C(and_3_out), .Q(DS2));  // open: nQ
  D_FF d_ff_4 (.D(multiplexer_4_out), .C(and_4_out), .Q(DS3));  // open: nQ

  // Other names for the same wires on the sheet: DIRECTION = DIR
endmodule
