// Digital circuit temp.dig as structural Verilog
module temp (
);

  wire button_1_out, d_ff_1_q, d_ff_2_q, d_ff_3_q, d_ff_4_q, dipswitch_1_out, dipswitch_2_out,
       dipswitch_3_out, dipswitch_4_out, dipswitch_5_out, dipswitch_6_out, dipswitch_7_out, dipswitch_8_out,
       dipswitch_9_out, dipswitch_10_out, dipswitch_11_out, dipswitch_12_out, dipswitch_13_out,
       multiplexer_1_out, multiplexer_2_out, multiplexer_3_out, multiplexer_4_out, stack_module_1_ds0,
       stack_module_1_ds1, stack_module_1_ds2, stack_module_1_ds3;

  Button button_1 (.out(button_1_out));
  DipSwitch dipswitch_1 (.out(dipswitch_1_out));
  DipSwitch dipswitch_2 (.out(dipswitch_2_out));
  DipSwitch dipswitch_3 (.out(dipswitch_3_out));
  DipSwitch dipswitch_4 (.out(dipswitch_4_out));
  DipSwitch dipswitch_5 (.out(dipswitch_5_out));
  DipSwitch dipswitch_6 (.out(dipswitch_6_out));
  DipSwitch dipswitch_7 (.out(dipswitch_7_out));
  DipSwitch dipswitch_8 (.out(dipswitch_8_out));
  DipSwitch #(.dipDefault("true")) dipswitch_9 (.out(dipswitch_9_out));
  DipSwitch #(.dipDefault("true")) dipswitch_10 (.out(dipswitch_10_out));
  DipSwitch #(.dipDefault("true")) dipswitch_11 (.out(dipswitch_11_out));
  DipSwitch #(.dipDefault("true")) dipswitch_12 (.out(dipswitch_12_out));
  DipSwitch dipswitch_13 (.out(dipswitch_13_out));
  stack_module stack_module_1 (
    .IN0(dipswitch_2_out), .IN1(dipswitch_3_out), .IN2(dipswitch_4_out), .IN3(dipswitch_5_out),
    .A(dipswitch_6_out), .B(dipswitch_7_out), .C(dipswitch_8_out), .CLOCK(button_1_out),
    .DS0_EN(dipswitch_9_out), .DS1_EN(dipswitch_10_out), .DS2_EN(dipswitch_11_out),
    .DS3_EN(dipswitch_12_out), .DS4(d_ff_1_q), .DIR(dipswitch_13_out), .DS3(stack_module_1_ds3),
    .DS2(stack_module_1_ds2), .DS1(stack_module_1_ds1), .DS0(stack_module_1_ds0));
  Multiplexer multiplexer_1 (
    .sel(dipswitch_13_out), .in_0(stack_module_1_ds3), .in_1(d_ff_2_q), .out(multiplexer_1_out));
  Multiplexer multiplexer_2 (.sel(dipswitch_13_out), .in_0(d_ff_1_q), .in_1(d_ff_3_q), .out(multiplexer_2_out));
  Multiplexer multiplexer_3 (.sel(dipswitch_13_out), .in_0(d_ff_2_q), .in_1(d_ff_4_q), .out(multiplexer_3_out));
  Multiplexer multiplexer_4 (.sel(dipswitch_13_out), .in_0(d_ff_3_q), .in_1(dipswitch_1_out), .out(multiplexer_4_out));
  D_FF d_ff_1 (.D(multiplexer_1_out), .C(button_1_out), .Q(d_ff_1_q));  // open: nQ
  D_FF d_ff_2 (.D(multiplexer_2_out), .C(button_1_out), .Q(d_ff_2_q));  // open: nQ
  D_FF d_ff_3 (.D(multiplexer_3_out), .C(button_1_out), .Q(d_ff_3_q));  // open: nQ
  D_FF d_ff_4 (.D(multiplexer_4_out), .C(button_1_out), .Q(d_ff_4_q));  // open: nQ
  LED led_1 (.in(stack_module_1_ds0));
  LED led_2 (.in(stack_module_1_ds1));
  LED led_3 (.in(stack_module_1_ds2));
  LED led_4 (.in(stack_module_1_ds3));
  LED led_5 (.in(d_ff_1_q));
  LED led_6 (.in(d_ff_2_q));
  LED led_7 (.in(d_ff_3_q));
  LED led_8 (.in(d_ff_4_q));
endmodule
