// Digital circuit vm-digital.dig as structural Verilog
module vm_digital (
  input  Clock,
  input  SC_ENABLE,
  output [15:0] out_3,
  output [15:0] out_4,
  output [15:0] out_5
);

  wire button_1_out, IR_gt, MAR_gt, or_1_out, PC_gt, PM_gt, RESET, Step_00, Step_01, Step_10, Step_11;
  wire [1:0] SC_OUT;
  wire [2:0] Instruction_Register__IR_q_2;
  wire [12:0] Instruction_Register__IR_q;
  wire [15:0] ADDR_MEM, Program_Counter__PC_out;

  Button u_RESET (.out(RESET));
  Button button_1 (.out(button_1_out));
  Register #(.Bits(16)) Instruction_Register__IR (
    .D(out_4), .C(Clock), .en(button_1_out), .Q({Instruction_Register__IR_q_2, Instruction_Register__IR_q}));
  or or_1 (or_1_out, RESET, Step_10);
  Decoder #(.Selector_Bits(2)) decoder_1 (
    .sel(SC_OUT), .out_0(Step_00), .out_1(Step_01), .out_2(Step_10), .out_3(Step_11));
  CounterPreset #(.Bits(16)) Memory_Access_Register__MAR (
    .en(1'b1), .C(Clock), .dir(1'b1), .in(out_4), .ld(1'b0), .clr(RESET), .out(ADDR_MEM));  // open: ovf
  ROM #(.AddrBits(16), .Bits(16), .isProgramMemory("true")) Program_Memory__PM (.A(ADDR_MEM), .sel(PM_gt), .D(out_3));
  CounterPreset #(.Bits(16)) Program_Counter__PC (
    .en(Step_10), .C(Clock), .dir(1'b0), .in(out_4), .ld(1'b0), .clr(RESET), .out(Program_Counter__PC_out));  // open: ovf
  Counter #(.Bits(2)) Step_Counter__SC (.en(SC_ENABLE), .C(Clock), .clr(or_1_out), .out(SC_OUT));  // open: ovf
  assign out_4 = PC_gt ? Program_Counter__PC_out : 16'bz;  // Driver driver_1
  assign out_4 = MAR_gt ? ADDR_MEM : 16'bz;  // Driver driver_2
  assign out_4 = PM_gt ? out_3 : 16'bz;  // Driver driver_3
  Decoder #(.Selector_Bits(3)) decoder_2 (
    .sel(Instruction_Register__IR_q_2), .out_0(MAR_gt), .out_1(PM_gt), .out_2(PC_gt), .out_7(IR_gt));  // open: out_3, out_4, out_5, out_6

  assign out_5 = out_4;

  // Other names for the same wires on the sheet: CLK = Clock; DATA_BUS[15:0] = out_4; SC_EN = SC_ENABLE

  // Notes on the sheet:
  //   SC_ENABLE: default 1
  //   contents of Program_Memory__PM (hex, n*v repeats v):
  //   0,2,4,6,8,a,c,e,10,12,14,16,18,1a,1c,1e,0,2,4,6,8,a,c,e,10,12
  //   ,14,16,18,1a,1c,1e,0,2,4,6,8,a,c,e,10,12,14,16,18,1a,1c,1e,0,2
  //   ,4,6,8,a,c,e,10,12,14,16,18,1a,1c,1e,0,2,4,6,8,a,c,e,10,12,14
  //   ,16,18,1a,1c,1e,0,2,4,6,8,a,c,e,10,12,14,16,18,1a,1c,1e,0,2,4
  //   ,6,8,a,c,e,10,12,14,16,18,1a,1c,1e,0,2,4,6,8,a,c,e,10,12,14,16
  //   ,18,1a,1c,1e,0,2,4,6,8,a,c,e,10,12,14,16,18,1a,1c,1e,0,2,4,6,8
  //   ,a,c,e,10,12,14,16,18,1a,1c,1e,0,2,4,6,8,a,c,e,10,12,14,16,18
  //   ,1a,1c,1e,0,2,4,6,8,a,c,e,10,12,14,16,18,1a,1c,1e,0,2,4,6,8,a
  //   ,c,e,10,12,14,16,18,1a,1c,1e,0,2,4,6,8,a,c,e,10,12,14,16,18,1a
  //   ,1c,1e,0,2,4,6,8,a,c,e,10,12,14,16,18,1a,1c,1e,0,2,4,6,8,a,c,e
  //   ,10,12,14,16,18,1a,1c,1e,0,2,4,6,8,a,c,e,10,12,14,16,18,1a,1c
  //   ,1e,0,2,4,6,8,a,c,e,10,12,14,16,18,1a,1c,1e,0,2,4,6,8,a,c,e,10
  //   ,12,14,16,18,1a,1c,1e,0,2,4,6,8,a,c,e,10,12,14,16,18,1a,1c,1e
  //   ,0,2,4,6,8,a,c,e,10,12,14,16,18,1a,1c,1e,0,2,4,6,8,a,c,e,10,12
  //   ,14,16,18,1a,1c,1e,0,2,4,6,8,a,c,e,10,12,14,16,18,1a,1c,1e,0,2
  //   ,4,6,8,a,c,e,10,12,14,16,18,1a,1c,1e,0,2,4,6,8,a,c,e,10,12,14
  //   ,16,18,1a,1c,1e,0,2,4,6,8,a,c,e,10,12,14,16,18,1a,1c,1e,0,2,4
  //   ,6,8,a,c,e,10,12,14,16,18,1a,1c,1e,0,2,4,6,8,a,c,e,10,12,14,16
  //   ,18,1a,1c,1e,0,2,4,6,8,a,c,e,10,12,14,16,18,1a,1c,1e,0,2,4,6,8
  //   ,a,c,e,10,12,14,16,18,1a,1c,1e,0,2,4,6,8,a,c,e,10,12,14,16,18
  //   ,1a,1c,1e,0,2,4,6,8,a,c,e,10,12,14,16,18,1a,1c,1e,0,2,4,6,8,a
  //   ,c,e,10,12,14,16,18,1a,1c,1e
endmodule
